// Logisim project APNP 10 - Memória 4 X 8 - Layla Couto.circ as structural Verilog: 1 circuit, main circuit main
module main (
  input  [7:0] Entrada,
  input  [1:0] \Endereço ,
  input  CS,
  input  RD,
  input  CE,
  output [7:0] \Saída 
);

  wire and_1_out, and_2_out, and_3_out, and_4_out, and_5_out, and_6_out, and_7_out, and_8_out, and_9_out,
       and_10_out, and_11_out, and_12_out, and_13_out, and_14_out, and_15_out, and_16_out, and_17_out,
       and_18_out, and_19_out, and_20_out, and_21_out, and_22_out, and_23_out, and_24_out, and_25_out,
       and_26_out, and_27_out, and_28_out, and_29_out, and_30_out, and_31_out, and_32_out, and_33_out,
       and_34_out, and_35_out, and_36_out, and_37_out, and_38_out, and_39_out, and_40_out, and_41_out,
       and_42_out, d_ff_1_q, d_ff_2_q, d_ff_3_q, d_ff_4_q, d_ff_5_q, d_ff_6_q, d_ff_7_q, d_ff_8_q, d_ff_9_q,
       d_ff_10_q, d_ff_11_q, d_ff_12_q, d_ff_13_q, d_ff_14_q, d_ff_15_q, d_ff_16_q, d_ff_17_q, d_ff_18_q,
       d_ff_19_q, d_ff_20_q, d_ff_21_q, d_ff_22_q, d_ff_23_q, d_ff_24_q, d_ff_25_q, d_ff_26_q, d_ff_27_q,
       d_ff_28_q, d_ff_29_q, d_ff_30_q, d_ff_31_q, d_ff_32_q, not_1_out, not_2_out, not_3_out, not_4_out,
       not_5_out;
  wire [7:0] or_8_out;

  not not_1 (not_1_out, \Endereço [0]);
  and and_1 (and_1_out, not_1_out, not_2_out);
  not not_2 (not_2_out, \Endereço [1]);
  and and_2 (and_2_out, \Endereço [0], not_3_out);
  not not_3 (not_3_out, \Endereço [1]);
  not not_4 (not_4_out, \Endereço [0]);
  and and_3 (and_3_out, not_4_out, \Endereço [1]);
  and and_4 (and_4_out, \Endereço [0], \Endereço [1]);
  and and_5 (and_5_out, CS, not_5_out);
  not not_5 (not_5_out, RD);
  and and_6 (and_6_out, CS, RD, CE);
  and and_7 (and_7_out, and_1_out, and_5_out);
  and and_8 (and_8_out, and_2_out, and_5_out);
  and and_9 (and_9_out, and_3_out, and_5_out);
  and and_10 (and_10_out, and_4_out, and_5_out);
  D_Flip_Flop d_ff_1 (.clk(and_7_out), .D(Entrada[7]), .Q(d_ff_1_q));  // open: Qn, preset, en, reset
  and and_11 (and_11_out, and_1_out, d_ff_1_q);
  D_Flip_Flop d_ff_2 (.clk(and_8_out), .D(Entrada[7]), .Q(d_ff_2_q));  // open: Qn, preset, en, reset
  and and_12 (and_12_out, and_2_out, d_ff_2_q);
  D_Flip_Flop d_ff_3 (.clk(and_9_out), .D(Entrada[7]), .Q(d_ff_3_q));  // open: Qn, preset, en, reset
  and and_13 (and_13_out, and_3_out, d_ff_3_q);
  D_Flip_Flop d_ff_4 (.clk(and_10_out), .D(Entrada[7]), .Q(d_ff_4_q));  // open: Qn, preset, en, reset
  and and_14 (and_14_out, and_4_out, d_ff_4_q);
  or or_1 (or_8_out[7], and_14_out, and_13_out, and_12_out, and_11_out);
  D_Flip_Flop d_ff_5 (.clk(and_7_out), .D(Entrada[6]), .Q(d_ff_5_q));  // open: Qn, preset, en, reset
  and and_15 (and_15_out, and_1_out, d_ff_5_q);
  D_Flip_Flop d_ff_6 (.clk(and_8_out), .D(Entrada[6]), .Q(d_ff_6_q));  // open: Qn, preset, en, reset
  and and_16 (and_16_out, and_2_out, d_ff_6_q);
  D_Flip_Flop d_ff_7 (.clk(and_9_out), .D(Entrada[6]), .Q(d_ff_7_q));  // open: Qn, preset, en, reset
  and and_17 (and_17_out, and_3_out, d_ff_7_q);
  D_Flip_Flop d_ff_8 (.clk(and_10_out), .D(Entrada[6]), .Q(d_ff_8_q));  // open: Qn, preset, en, reset
  and and_18 (and_18_out, and_4_out, d_ff_8_q);
  or or_2 (or_8_out[6], and_18_out, and_17_out, and_16_out, and_15_out);
  D_Flip_Flop d_ff_9 (.clk(and_7_out), .D(Entrada[5]), .Q(d_ff_9_q));  // open: Qn, preset, en, reset
  and and_19 (and_19_out, and_1_out, d_ff_9_q);
  D_Flip_Flop d_ff_10 (.clk(and_8_out), .D(Entrada[5]), .Q(d_ff_10_q));  // open: Qn, preset, en, reset
  and and_20 (and_20_out, and_2_out, d_ff_10_q);
  D_Flip_Flop d_ff_11 (.clk(and_9_out), .D(Entrada[5]), .Q(d_ff_11_q));  // open: Qn, preset, en, reset
  and and_21 (and_21_out, and_3_out, d_ff_11_q);
  D_Flip_Flop d_ff_12 (.clk(and_10_out), .D(Entrada[5]), .Q(d_ff_12_q));  // open: Qn, preset, en, reset
  and and_22 (and_22_out, and_4_out, d_ff_12_q);
  or or_3 (or_8_out[5], and_22_out, and_21_out, and_20_out, and_19_out);
  D_Flip_Flop d_ff_13 (.clk(and_7_out), .D(Entrada[4]), .Q(d_ff_13_q));  // open: Qn, preset, en, reset
  and and_23 (and_23_out, and_1_out, d_ff_13_q);
  D_Flip_Flop d_ff_14 (.clk(and_8_out), .D(Entrada[4]), .Q(d_ff_14_q));  // open: Qn, preset, en, reset
  and and_24 (and_24_out, and_2_out, d_ff_14_q);
  D_Flip_Flop d_ff_15 (.clk(and_9_out), .D(Entrada[4]), .Q(d_ff_15_q));  // open: Qn, preset, en, reset
  and and_25 (and_25_out, and_3_out, d_ff_15_q);
  D_Flip_Flop d_ff_16 (.clk(and_10_out), .D(Entrada[4]), .Q(d_ff_16_q));  // open: Qn, preset, en, reset
  and and_26 (and_26_out, and_4_out, d_ff_16_q);
  or or_4 (or_8_out[4], and_26_out, and_25_out, and_24_out, and_23_out);
  D_Flip_Flop d_ff_17 (.clk(and_7_out), .D(Entrada[3]), .Q(d_ff_17_q));  // open: Qn, preset, en, reset
  and and_27 (and_27_out, and_1_out, d_ff_17_q);
  D_Flip_Flop d_ff_18 (.clk(and_8_out), .D(Entrada[3]), .Q(d_ff_18_q));  // open: Qn, preset, en, reset
  and and_28 (and_28_out, and_2_out, d_ff_18_q);
  D_Flip_Flop d_ff_19 (.clk(and_9_out), .D(Entrada[3]), .Q(d_ff_19_q));  // open: Qn, preset, en, reset
  and and_29 (and_29_out, and_3_out, d_ff_19_q);
  D_Flip_Flop d_ff_20 (.clk(and_10_out), .D(Entrada[3]), .Q(d_ff_20_q));  // open: Qn, preset, en, reset
  and and_30 (and_30_out, and_4_out, d_ff_20_q);
  or or_5 (or_8_out[3], and_30_out, and_29_out, and_28_out, and_27_out);
  D_Flip_Flop d_ff_21 (.clk(and_7_out), .D(Entrada[2]), .Q(d_ff_21_q));  // open: Qn, preset, en, reset
  and and_31 (and_31_out, and_1_out, d_ff_21_q);
  D_Flip_Flop d_ff_22 (.clk(and_8_out), .D(Entrada[2]), .Q(d_ff_22_q));  // open: Qn, preset, en, reset
  and and_32 (and_32_out, and_2_out, d_ff_22_q);
  D_Flip_Flop d_ff_23 (.clk(and_9_out), .D(Entrada[2]), .Q(d_ff_23_q));  // open: Qn, preset, en, reset
  and and_33 (and_33_out, and_3_out, d_ff_23_q);
  D_Flip_Flop d_ff_24 (.clk(and_10_out), .D(Entrada[2]), .Q(d_ff_24_q));  // open: Qn, preset, en, reset
  and and_34 (and_34_out, and_4_out, d_ff_24_q);
  or or_6 (or_8_out[2], and_34_out, and_33_out, and_32_out, and_31_out);
  assign \Saída  = and_6_out ? or_8_out : 8'bz;  // Controlled_Buffer controlled_buffer_1
  D_Flip_Flop d_ff_25 (.clk(and_7_out), .D(Entrada[1]), .Q(d_ff_25_q));  // open: Qn, preset, en, reset
  and and_35 (and_35_out, and_1_out, d_ff_25_q);
  D_Flip_Flop d_ff_26 (.clk(and_8_out), .D(Entrada[1]), .Q(d_ff_26_q));  // open: Qn, preset, en, reset
  and and_36 (and_36_out, and_2_out, d_ff_26_q);
  D_Flip_Flop d_ff_27 (.clk(and_9_out), .D(Entrada[1]), .Q(d_ff_27_q));  // open: Qn, preset, en, reset
  and and_37 (and_37_out, and_3_out, d_ff_27_q);
  D_Flip_Flop d_ff_28 (.clk(and_10_out), .D(Entrada[1]), .Q(d_ff_28_q));  // open: Qn, preset, en, reset
  and and_38 (and_38_out, and_4_out, d_ff_28_q);
  or or_7 (or_8_out[1], and_38_out, and_37_out, and_36_out, and_35_out);
  D_Flip_Flop d_ff_29 (.clk(and_7_out), .D(Entrada[0]), .Q(d_ff_29_q));  // open: Qn, preset, en, reset
  and and_39 (and_39_out, and_1_out, d_ff_29_q);
  D_Flip_Flop d_ff_30 (.clk(and_8_out), .D(Entrada[0]), .Q(d_ff_30_q));  // open: Qn, preset, en, reset
  and and_40 (and_40_out, and_2_out, d_ff_30_q);
  D_Flip_Flop d_ff_31 (.clk(and_9_out), .D(Entrada[0]), .Q(d_ff_31_q));  // open: Qn, preset, en, reset
  and and_41 (and_41_out, and_3_out, d_ff_31_q);
  D_Flip_Flop d_ff_32 (.clk(and_10_out), .D(Entrada[0]), .Q(d_ff_32_q));  // open: Qn, preset, en, reset
  and and_42 (and_42_out, and_4_out, d_ff_32_q);
  or or_8 (or_8_out[0], and_42_out, and_41_out, and_40_out, and_39_out);
endmodule
