// Logisim project APNP 3 - Aula 2.circ as structural Verilog: 1 circuit, main circuit main
module main (
  input  A,
  input  B,
  input  A_2,
  input  B_2,
  input  C,
  input  D,
  input  A_3,
  input  B_3,
  input  C_2,
  input  D_2,
  input  A_4,
  input  B_4,
  input  C_3,
  input  D_3,
  input  E,
  input  A_5,
  input  B_5,
  input  C_4,
  input  D_4,
  input  E_2,
  output out_21,
  output out_22,
  output out_23,
  output out_24,
  output out_25
);

  wire and_2_out, and_3_out, and_4_out, and_5_out, and_6_out, and_9_out, or_1_out, or_2_out, or_4_out,
       or_5_out;

  and and_1 (out_21, A, B);
  and and_2 (and_2_out, A_2, B_2);
  and and_3 (and_3_out, C, D);
  and and_4 (and_4_out, A_3, B_3);
  or or_1 (or_1_out, B_4, C_3);
  or or_2 (or_2_out, D_3, E);
  and and_5 (and_5_out, A_5, B_5);
  or or_3 (out_22, and_2_out, and_3_out);
  or or_4 (or_4_out, and_4_out, C_2);
  and and_6 (and_6_out, A_4, or_1_out);
  or or_5 (or_5_out, and_5_out, C_4);
  and and_7 (out_23, or_4_out, D_2);
  and and_8 (out_24, and_6_out, or_2_out);
  and and_9 (and_9_out, or_5_out, D_4);
  or or_6 (out_25, and_9_out, E_2);

  // Notes on the sheet:
  //   Y = A . B
  //   Y = (A . B) + (C . D)
  //   Y = A . B + C .D
  //   Y = A . (B + C) . (D +E)
  //   Y = A . B + C . D +E
endmodule
