// Logisim project APNP 3 - Aula 3 - Maxtermo e Mintermo.circ as structural Verilog: 1 circuit, main circuit main
module main (
  input  A,
  input  B,
  input  C,
  input  A_2,
  input  B_2,
  input  C_2,
  output out_7,
  output out_8
);

  wire and_1_out, and_2_out, and_3_out, and_4_out, not_1_out, not_2_out, not_3_out, not_4_out, not_5_out,
       not_6_out, or_1_out, or_2_out, or_3_out, or_4_out;

  not not_1 (not_1_out, A);
  not not_2 (not_2_out, B);
  not not_3 (not_3_out, C);
  not not_4 (not_4_out, A_2);
  not not_5 (not_5_out, B_2);
  not not_6 (not_6_out, C_2);
  or or_1 (or_1_out, A, B, C);
  or or_2 (or_2_out, A, B, not_3_out);
  or or_3 (or_3_out, A, not_2_out, C);
  or or_4 (or_4_out, not_1_out, B, C);
  and and_1 (and_1_out, not_4_out, B_2, C_2);
  and and_2 (and_2_out, A_2, not_5_out, C_2);
  and and_3 (and_3_out, A_2, B_2, not_6_out);
  and and_4 (and_4_out, A_2, B_2, C_2);
  and and_5 (out_7, or_1_out, or_2_out, or_3_out, or_4_out);
  or or_5 (out_8, and_1_out, and_2_out, and_3_out, and_4_out);

  // Notes on the sheet:
  //   Maxtermo
  //   Mintermo
  //   S = (A + B + C) . (A + B +C' ) . (A + B' + C) . (A' + B + C)
  //   S = (A' . B . C) + (A . B' . C ) + (A . B . C') + (A . B . C)
endmodule
