// Logisim project APNP 5 - Exemplo aula.circ as structural Verilog: 2 circuits, main circuit main
module main (
  input  A,
  input  B,
  input  C,
  input  D,
  output out_5
);

  wire and_1_out, and_2_out, and_3_out, and_4_out, not_1_out, not_2_out, not_3_out;

  not not_1 (not_1_out, A);
  not not_2 (not_2_out, B);
  not not_3 (not_3_out, C);
  // NOT_Gate not_4 has open pins: in=D, out=open
  and and_1 (and_1_out, not_2_out, not_3_out);
  and and_2 (and_2_out, A, not_2_out);
  and and_3 (and_3_out, not_1_out, B);
  and and_4 (and_4_out, A, C);
  _7_Segment_Display u_7_segment_display_1 (.c(out_5));  // open: g, f, a, b, e, d, dp
  or or_1 (out_5, D, and_1_out, and_2_out, and_3_out, and_4_out);

  // Notes on the sheet:
  //   Exemplo 1 Circuito do Display de 7 segmentos
  //   S = D + B'C' + AB' + A'B + AC
endmodule

module C1 (
  input  A,
  input  B,
  input  C,
  input  D
);

  wire main_1_out_5;

  main main_1 (.A(A), .B(B), .C(C), .D(D), .out_5(main_1_out_5));
  _7_Segment_Display u_7_segment_display_1 (.c(main_1_out_5));  // open: g, f, a, b, e, d, dp
endmodule
