// Logisim project APNP 5 - Lista 4 - OAC.circ as structural Verilog: 9 circuits, main circuit main
module main (
  input  A,
  input  B,
  input  C,
  input  D
);

  wire c1_1_out_5, c2_1_out_5, c3_1_out_5, c4_1_out_5, c5_1_out_5, c6_1_out_5, c7_1_out_5, c8_1_out_5;

  C7 c7_1 (.A(A), .B(B), .C(C), .D(D), .out_5(c7_1_out_5));
  C6 c6_1 (.A(A), .B(B), .C(C), .D(D), .out_5(c6_1_out_5));
  C5 c5_1 (.A(A), .B(B), .C(C), .D(D), .out_5(c5_1_out_5));
  C4 c4_1 (.A(A), .B(B), .C(C), .D(D), .out_5(c4_1_out_5));
  C3 c3_1 (.A(A), .B(B), .C(C), .D(D), .out_5(c3_1_out_5));
  C2 c2_1 (.A(A), .B(B), .C(C), .D(D), .out_5(c2_1_out_5));
  C1 c1_1 (.A(A), .B(B), .C(C), .D(D), .out_5(c1_1_out_5));
  C8 c8_1 (.A(A), .B(B), .C(C), .D(D), .out_5(c8_1_out_5));
  _7_Segment_Display u_7_segment_display_1 (.b(c8_1_out_5), .c(c8_1_out_5));  // open: g, f, a, e, d, dp
  _7_Segment_Display u_7_segment_display_2 (
    .g(c4_1_out_5), .f(c5_1_out_5), .a(c6_1_out_5), .b(c7_1_out_5), .e(c3_1_out_5), .d(c2_1_out_5),
    .c(c1_1_out_5));  // open: dp

  // Notes on the sheet:
  //   Display de 7 segmentos
endmodule

module C1 (
  input  A,
  input  B,
  input  C,
  input  D,
  output out_5
);

  wire and_1_out, and_2_out, and_3_out, not_1_out, not_2_out, not_3_out;

  not not_1 (not_1_out, A);
  not not_2 (not_2_out, B);
  not not_3 (not_3_out, C);
  // NOT_Gate not_4 has open pins: in=D, out=open
  and and_1 (and_1_out, A, not_2_out);
  and and_2 (and_2_out, not_1_out, not_3_out);
  and and_3 (and_3_out, B, C);
  or or_1 (out_5, D, and_1_out, and_2_out, and_3_out);
  _7_Segment_Display u_7_segment_display_1 (.c(out_5));  // open: g, f, a, b, e, d, dp

  // Notes on the sheet:
  //   S = D + AB' + A'C' + BC
endmodule

module C2 (
  input  A,
  input  B,
  input  C,
  input  D,
  output out_5
);

  wire and_1_out, and_2_out, and_3_out, and_4_out, and_5_out, and_6_out, not_1_out, not_2_out, not_3_out,
       not_4_out;

  not not_1 (not_1_out, A);
  not not_2 (not_2_out, B);
  not not_3 (not_3_out, C);
  not not_4 (not_4_out, D);
  and and_1 (and_1_out, not_2_out, not_4_out);
  and and_2 (and_2_out, A, B, not_3_out);
  and and_3 (and_3_out, not_1_out, not_2_out, C);
  and and_4 (and_4_out, A, B, D);
  and and_5 (and_5_out, not_1_out, C, not_4_out);
  and and_6 (and_6_out, B, not_3_out, D);
  or or_1 (out_5, and_1_out, and_2_out, and_3_out, and_4_out, and_5_out, and_6_out);
  _7_Segment_Display u_7_segment_display_1 (.d(out_5));  // open: g, f, a, b, e, c, dp

  // Notes on the sheet:
  //   S = B'D' + ABC' + A'B'C + ABD  + A'CD' + BC'D
endmodule

module C3 (
  input  A,
  input  B,
  input  C,
  input  D,
  output out_5
);

  wire and_1_out, and_2_out, and_3_out, not_1_out, not_2_out, not_3_out, not_4_out;

  not not_1 (not_1_out, A);
  not not_2 (not_2_out, B);
  not not_3 (not_3_out, C);
  not not_4 (not_4_out, D);
  and and_1 (and_1_out, not_2_out, not_4_out);
  and and_2 (and_2_out, A, not_3_out, not_4_out);
  and and_3 (and_3_out, not_1_out, C, not_4_out);
  _7_Segment_Display u_7_segment_display_1 (.e(out_5));  // open: g, f, a, b, d, c, dp
  or or_1 (out_5, and_1_out, and_2_out, and_3_out);

  // Notes on the sheet:
  //   S = B'D' + AC'D' + A'CD'
endmodule

module C4 (
  input  A,
  input  B,
  input  C,
  input  D,
  output out_5
);

  wire and_1_out, and_2_out, and_3_out, and_4_out, and_5_out, not_1_out, not_2_out, not_3_out, not_4_out;

  not not_1 (not_1_out, A);
  not not_2 (not_2_out, B);
  not not_3 (not_3_out, C);
  not not_4 (not_4_out, D);
  and and_1 (and_1_out, A, B);
  and and_2 (and_2_out, B, not_3_out);
  and and_3 (and_3_out, B, not_4_out);
  and and_4 (and_4_out, A, not_3_out);
  and and_5 (and_5_out, not_1_out, not_2_out, C);
  or or_1 (out_5, and_1_out, and_2_out, and_3_out, and_4_out, and_5_out);
  _7_Segment_Display u_7_segment_display_1 (.g(out_5));  // open: f, a, b, e, d, c, dp

  // Notes on the sheet:
  //   S = AB + BC' + BD' + AC' + A'B'C
endmodule

module C5 (
  input  A,
  input  B,
  input  C,
  input  D,
  output out_5
);

  wire and_1_out, and_2_out, and_3_out, and_4_out, and_5_out, not_1_out, not_2_out, not_3_out, not_4_out;

  not not_1 (not_1_out, A);
  not not_2 (not_2_out, B);
  not not_3 (not_3_out, C);
  not not_4 (not_4_out, D);
  and and_1 (and_1_out, not_1_out, B);
  and and_2 (and_2_out, B, C);
  and and_3 (and_3_out, A, not_2_out, not_3_out);
  and and_4 (and_4_out, not_1_out, not_3_out, not_4_out);
  and and_5 (and_5_out, A, C, not_4_out);
  or or_1 (out_5, and_1_out, and_2_out, and_3_out, and_4_out, and_5_out);
  _7_Segment_Display u_7_segment_display_1 (.f(out_5));  // open: g, a, b, e, d, c, dp

  // Notes on the sheet:
  //   S = A'B + BC + AB'C' + A'C'D' + ACD'
endmodule

module C6 (
  input  A,
  input  B,
  input  C,
  input  D,
  output out_5
);

  wire and_1_out, and_2_out, and_3_out, and_4_out, not_1_out, not_2_out, not_3_out, not_4_out;

  not not_1 (not_1_out, A);
  not not_2 (not_2_out, B);
  not not_3 (not_3_out, C);
  not not_4 (not_4_out, D);
  and and_1 (and_1_out, B, D);
  and and_2 (and_2_out, A, not_3_out);
  and and_3 (and_3_out, not_1_out, C);
  and and_4 (and_4_out, not_2_out, not_4_out);
  _7_Segment_Display u_7_segment_display_1 (.a(out_5));  // open: g, f, b, e, d, c, dp
  or or_1 (out_5, and_1_out, and_2_out, and_3_out, and_4_out);

  // Notes on the sheet:
  //   S = BD + AC' + A'C + B'D'
endmodule

module C7 (
  input  A,
  input  B,
  input  C,
  input  D,
  output out_5
);

  wire and_1_out, and_2_out, and_3_out, and_4_out, and_5_out, not_1_out, not_2_out, not_3_out, not_4_out;

  not not_1 (not_1_out, A);
  not not_2 (not_2_out, B);
  not not_3 (not_3_out, C);
  not not_4 (not_4_out, D);
  buf and_1 (and_1_out, not_2_out);  // AND_Gate
  and and_2 (and_2_out, A, not_3_out);
  and and_3 (and_3_out, A, not_4_out);
  and and_4 (and_4_out, not_3_out, not_4_out);
  and and_5 (and_5_out, not_1_out, C, D);
  or or_1 (out_5, and_1_out, and_2_out, and_3_out, and_4_out, and_5_out);
  _7_Segment_Display u_7_segment_display_1 (.a(out_5));  // open: g, f, b, e, d, c, dp

  // Notes on the sheet:
  //   S = B' + AC' + AD' + C'D' + A'CD
endmodule

module C8 (
  input  A,
  input  B,
  input  C,
  input  D,
  output out_5
);

  wire and_1_out, and_2_out;

  // NOT_Gate not_1 has open pins: in=A, out=open
  // NOT_Gate not_2 has open pins: in=B, out=open
  // NOT_Gate not_3 has open pins: in=C, out=open
  // NOT_Gate not_4 has open pins: in=D, out=open
  and and_1 (and_1_out, A, B);
  and and_2 (and_2_out, A, C);
  or or_1 (out_5, and_1_out, and_2_out);
  _7_Segment_Display u_7_segment_display_1 (.b(out_5));  // open: g, f, a, e, d, c, dp

  // Notes on the sheet:
  //   S = AB + AC
endmodule
