// Logisim project APNP 8 - Lista - Layla Couto.circ as structural Verilog: 2 circuits, main circuit main
module main (
  input  in_1,
  input  in_2,
  input  in_3,
  input  in_4,
  input  in_5,
  input  in_6,
  input  in_7,
  input  in_8,
  input  in_9,
  input  in_10,
  input  in_11,
  input  in_12,
  input  in_13,
  input  in_14,
  input  in_15,
  input  in_16,
  output out_17,
  output out_18,
  output out_19,
  output out_20,
  output out_21,
  output out_22,
  output out_23,
  output out_24,
  output out_25
);

  wire bit0_vai_um, bit1_vai_um, bit2_vai_um, bit3_vai_um, bit4_vai_um, bit5_vai_um, bit6_vai_um;

  Somador bit0 (.A(in_8), .B(in_9), .Vem_Um(1'b0), .Soma(out_25), .Vai_Um(bit0_vai_um));
  Somador bit1 (.A(in_7), .B(in_16), .Vem_Um(bit0_vai_um), .Soma(out_24), .Vai_Um(bit1_vai_um));
  Somador bit2 (.A(in_6), .B(in_15), .Vem_Um(bit1_vai_um), .Soma(out_23), .Vai_Um(bit2_vai_um));
  Somador bit3 (.A(in_5), .B(in_14), .Vem_Um(bit2_vai_um), .Soma(out_22), .Vai_Um(bit3_vai_um));
  Somador bit4 (.A(in_4), .B(in_13), .Vem_Um(bit3_vai_um), .Soma(out_21), .Vai_Um(bit4_vai_um));
  Somador bit5 (.A(in_3), .B(in_12), .Vem_Um(bit4_vai_um), .Soma(out_20), .Vai_Um(bit5_vai_um));
  Somador bit6 (.A(in_2), .B(in_11), .Vem_Um(bit5_vai_um), .Soma(out_19), .Vai_Um(bit6_vai_um));
  Somador bit7 (.A(in_1), .B(in_10), .Vem_Um(bit6_vai_um), .Soma(out_18), .Vai_Um(out_17));
endmodule

module Somador (
  input  A,
  input  B,
  input  Vem_Um,
  output Soma,
  output Vai_Um
);

  wire and_1_out, and_2_out, and_3_out, and_4_out, and_5_out, and_6_out, and_7_out, not_1_out, not_2_out,
       not_3_out;

  not not_1 (not_1_out, A);
  not not_2 (not_2_out, B);
  not not_3 (not_3_out, Vem_Um);
  and and_1 (and_1_out, not_1_out, not_2_out, Vem_Um);
  and and_2 (and_2_out, not_1_out, B, not_3_out);
  and and_3 (and_3_out, A, not_2_out, not_3_out);
  and and_4 (and_4_out, A, B, Vem_Um);
  and and_5 (and_5_out, A, B);
  and and_6 (and_6_out, A, Vem_Um);
  and and_7 (and_7_out, B, Vem_Um);
  or or_1 (Soma, and_1_out, and_2_out, and_3_out, and_4_out);
  or or_2 (Vai_Um, and_5_out, and_6_out, and_7_out);
endmodule
