// Logisim project APNP Semana 3 - Lista 2 - Layla Couto.circ as structural Verilog: 1 circuit, main circuit main
module main (
  input  A,
  input  B,
  input  C,
  input  A_2,
  input  B_2,
  input  C_2,
  input  A_3,
  input  B_3,
  input  C_3,
  output out_10,
  output out_11,
  output out_12
);

  wire not_1_out, not_2_out, not_3_out, not_4_out, not_5_out, not_6_out, not_7_out, not_8_out, not_9_out,
       or_1_out, or_2_out, or_3_out, or_4_out, or_5_out, or_6_out, or_7_out, or_8_out, or_9_out, or_10_out,
       or_11_out;

  not not_1 (not_1_out, A);
  not not_2 (not_2_out, B);
  not not_3 (not_3_out, C);
  not not_4 (not_4_out, A_2);
  not not_5 (not_5_out, B_2);
  not not_6 (not_6_out, C_2);
  not not_7 (not_7_out, A_3);
  not not_8 (not_8_out, B_3);
  not not_9 (not_9_out, C_3);
  or or_1 (or_1_out, A, B, C);
  or or_2 (or_2_out, A, not_2_out, C);
  or or_3 (or_3_out, not_1_out, not_2_out, not_3_out);
  or or_4 (or_4_out, A_2, B_2, C_2);
  or or_5 (or_5_out, A_2, not_5_out, not_6_out);
  or or_6 (or_6_out, not_4_out, B_2, not_6_out);
  or or_7 (or_7_out, not_4_out, not_5_out, C_2);
  or or_8 (or_8_out, not_7_out, not_8_out, not_9_out);
  or or_9 (or_9_out, not_7_out, B_3, not_9_out);
  or or_10 (or_10_out, A_3, not_8_out, not_9_out);
  or or_11 (or_11_out, A_3, B_3, not_9_out);
  and and_1 (out_10, or_1_out, or_2_out, or_3_out);
  and and_2 (out_11, or_4_out, or_5_out, or_6_out, or_7_out);
  and and_3 (out_12, or_8_out, or_9_out, or_10_out, or_11_out);

  // Notes on the sheet:
  //   Questão 1
  //   Questão 2
  //   Questão 3
  //   S = (A + B + C) . (A + B' + C) . (A' + B' + C')
  //   S = (A' . B' . C') + (A' . B . C') +(A . B' . C') +(A . B . C')
  //   S = (A + B + C) . (A + B' + C') . (A' + B + C') . (A' + B' + C)
endmodule
