// Logisim project APNP Semana 4 - Lista 3 - Layla Couto.circ as structural Verilog: 1 circuit, main circuit main
module main (
  input  A,
  input  B,
  input  C,
  input  A_2,
  input  B_2,
  input  C_2,
  input  A_3,
  input  B_3,
  input  C_3,
  input  C_4,
  input  A_4,
  input  B_4,
  input  C_5,
  output out_14,
  output out_15,
  output out_16,
  output out_17,
  output out_18
);

  wire and_1_out, and_2_out, and_3_out, and_4_out, and_5_out, and_6_out, and_7_out, and_8_out, and_9_out,
       and_10_out, and_11_out, and_12_out, and_13_out, and_14_out, not_1_out, not_2_out, not_3_out,
       not_4_out, not_5_out, not_6_out, not_7_out, not_8_out, not_9_out;

  not not_1 (not_1_out, A);
  not not_2 (not_2_out, B);
  not not_3 (not_3_out, C);
  not not_4 (not_4_out, A_2);
  not not_5 (not_5_out, C_2);
  not not_6 (not_6_out, A_3);
  not not_7 (not_7_out, B_3);
  not not_8 (not_8_out, C_3);
  not not_9 (not_9_out, C_4);
  and and_1 (and_1_out, A, not_3_out);
  and and_2 (and_2_out, A, not_2_out);
  and and_3 (and_3_out, not_2_out, C);
  and and_4 (and_4_out, not_1_out, C);
  buf and_5 (and_5_out, not_5_out);  // AND_Gate
  and and_6 (and_6_out, not_4_out, B_2);
  and and_7 (and_7_out, not_6_out, not_7_out, C_3);
  and and_8 (and_8_out, not_6_out, B_3, not_8_out);
  and and_9 (and_9_out, A_3, not_7_out, not_8_out);
  and and_10 (and_10_out, A_3, B_3, C_3);
  buf and_11 (and_11_out, not_9_out);  // AND_Gate
  and and_12 (and_12_out, A_4, C_5);
  and and_13 (and_13_out, B_4, C_5);
  and and_14 (and_14_out, A_4, B_4);
  buf or_1 (out_17, and_11_out);  // OR_Gate
  or or_2 (out_14, and_1_out, and_2_out, and_3_out, and_4_out);
  or or_3 (out_15, and_5_out, and_6_out);
  or or_4 (out_16, and_7_out, and_8_out, and_9_out, and_10_out);
  or or_5 (out_18, and_12_out, and_13_out, and_14_out);

  // Notes on the sheet:
  //   Questão 1
  //   Questão 2
  //   Questão 3
  //   Questão 4
  //   Questão 5
  //   S = C'
  //   S = C' + (A' . B) 
  //   S = (A . B) + (B . C) + (A . B)
  //   S = (A . C') + (A . B') + (B' . C) + (A' . C)
  //   S = (A' . B' . C) + (A' . B . C') + (A . B' . C') + (A . B . C)
endmodule
